# Fritzing sketch fritzing-sketch (saved by Fritzing 0.9.3b)
breadboards: 1

parts:
  M1 = Arduino NANO RP2040 CONNECT with headers
  S1 = Pushbutton [package="[THT]"]
  OLED1 = OLED Mono 0.56 inch blue or white  # not connected
  R1 = Resistor [tolerance=±5% resistance=220 package="0603 [SMD]"]  # not connected
  R2 = Resistor [tolerance=±5% resistance=220 package="0603 [SMD]"]
  U1 = POT [package=pot_alpha_rv16af-20]
  SP1 = SPEAKER [package=pcb_mount_speaker]

nets:
  N1: M1.GND-4, M1.GND-29, S1.Pin_3, S1.Pin_4, SP1.+
  N2: M1.D5, S1.Pin_1, S1.Pin_2
  N3: M1.D10, R2.Pin_1
  N4: R2.Pin_0, U1.A
  N5: U1.S, SP1.-

notes:
  Library: ggwave
  Example: arduino-rx
  Sample sketch for receiving and sending sound data with Arduino Nano RP2040 Connect
  The OLED display is optional.
  Press the button to retransmit the last received message.

custom parts:
  Arduino NANO RP2040 CONNECT with headers: Meet the only connected RP2040 board. It fits the Arduino Nano form factor, making it a small board with BIG features. The brain of the board is the Raspberry Pi RP2040 silicon; a dual-core Arm Cortex M0+ running at 133MHz. It has 264KB of SRAM, and the 16MB of flash memory is off-chip to give you extra storage. But what’s really exciting is the on-board connectivity options. The hugely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
  OLED Mono 0.56 inch blue or white: OLED, I2C 3.3V - 5V Blue and White text versions
