# Fritzing sketch fritzing-sketch (saved by Fritzing 0.9.3b)
breadboards: 1

parts:
  Part1 = Arduino Uno (Rev3)
  R1 = Resistor [tolerance=±5% resistance=220 package="0402 [SMD]"]
  LED1 = LED - 3mm [color="Red (633nm)" package="3 mm [THT]"]
  R2 = Resistor [tolerance=±5% resistance=220 package="0402 [SMD]"]
  R3 = Resistor [tolerance=±5% resistance=220 package="0402 [SMD]"]
  S1 = Pushbutton [package="[THT]"]
  S2 = Pushbutton [package="[THT]"]
  U1 = POT [package=pot_alpha_rv16af-20]
  J1 = Piezo Speaker

nets:
  N1: Part1.D10_PWM/SS, R1.Pin_0
  N2: Part1.D13/SCK, LED1.anode
  N3: Part1.GND, LED1.cathode, S1.Pin_1, S1.Pin_2, S2.Pin_1, S2.Pin_2, J1.pin1
  N4: Part1.D2, R3.Pin_1, S2.Pin_3, S2.Pin_4
  N5: Part1.D4, R2.Pin_1, S1.Pin_3, S1.Pin_4
  N6: Part1.5V, R2.Pin_0, R3.Pin_0
  N7: R1.Pin_1, U1.A
  N8: U1.S, J1.pin2

notes:
  Library: ggwave
  Example: arduino-tx
  Sample sketch for sending sound data with Arduino Uno Rev3
  Press button 1 to increase the counter.
  Press button 2 to transmit the counter value and reset it.
