# Fritzing sketch fritzing-sketch (saved by Fritzing 0.9.5d)
breadboards: 1

parts:
  Part1 = Adafruit MAX9814 Electret Microphone Amplifier [part_number="Adafruit #1713"]
  Pico_H2 = Raspberry Pi Pico H

nets:
  GND: Part1.GND, Pico_H2.GND
  VDD: Part1.VDD, Pico_H2.3V3
  N1: Part1.OUTPUT, Pico_H2.GP26_A0

notes:
  Library: ggwave
  Example: rp2040-rx
  Sample sketch for receiving sound data with RP2040.
  Tested with Raspberry Pi Pico board and analog mics.
  Compatible microphones:
  - MAX9814 (Analog)
  - KY-037 (Analog)
  - KY-038 (Analog)
  - WS Sound Sensor (Analog)

custom parts:
  Adafruit MAX9814 Electret Microphone Amplifier: Add an ear to your project with this well-designed electret microphone amplifier with AGC. This fully assembled and tested board comes with a 20-20KHz electret microphone soldered on. For the amplification, we use the Maxim MAX9814, a specialty chip that is designed for amplifying electret microphones in situations where the loudness of the audio isn't predictable. This fancy microphone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
  Raspberry Pi Pico H: Raspberry Pi Pico H. Based around the RP2040 microcontroller the Pico H is a low cost microcontroller device bringing Raspberry Pi quality, cost, and easy of use to the microcontroller space.
